# Fritzing sketch Arduino-Car (saved by Fritzing 0.9.3b)
breadboards: 1

parts:
  Componente1 = Arduino Uno (Rev3)
  Componente2 = Bluetooth HC-05 Macho
  hc-sr1 = hc-sr04
  IC1 = L293D [package=THT]
  M1 = DC Motor
  M2 = DC Motor
  VCC1 = Battery block 9V

nets:
  N1: Componente1.D9_PWM, IC1.In_2
  N2: Componente1.D10_PWM/SS, IC1.In_1
  N3: Componente1.D0/RX, Componente2.TXD
  N4: Componente1.D1/TX, Componente2.RXD
  N5: Componente1.D2, hc-sr1.Echo
  N6: Componente1.D3_PWM, hc-sr1.Trig
  N7: Componente1.D5_PWM, IC1.In_3
  N8: Componente1.D6_PWM, IC1.In_4
  VCC: Componente1.5V, Componente2.VCC, hc-sr1.VCC, IC1.Enable_1, IC1.Enable_2, IC1.+V
  GND: Componente1.GND, Componente2.GND, hc-sr1.GND, IC1.0V, VCC1.-
  N9: Componente1.VIN, IC1.+Vmotor, VCC1.+
  N10: IC1.Out_1_(_Controlled_by_Enable_1_), M1.pin_2
  N11: IC1.Out_2_(_Controlled_by_Enable_1_), M1.pin_1
  N12: IC1.Out_3_(_Controlled_by_Enable_2_), M2.pin_2
  N13: IC1.Out_4_(_Controlled_by_Enable_2_), M2.pin_1
